# Fritzing sketch Entrenador Arduino V1.0 (saved by Fritzing 0.9.3b)

parts:
  8x8_LED_matrix_MAX1 = 8x8 Red 8x8 LED Matrix with MAX7219
  8x8_LED_matrix_MAX2 = 8x8 Red 8x8 LED Matrix with MAX7219
  Componente1 = Arduino Nano (Rev3.0) (ICSP)
  VCC1 = Battery block 9V
  S1 = Toggle Switch [package=THT]

nets:
  VCC: 8x8_LED_matrix_MAX1.VCC, 8x8_LED_matrix_MAX2.VCC, 8x8_LED_matrix_MAX2.VCC_PT, Componente1.5V
  N1: 8x8_LED_matrix_MAX1.GND, 8x8_LED_matrix_MAX1.CLK_PT, 8x8_LED_matrix_MAX2.GND_PT, 8x8_LED_matrix_MAX2.CLK, Componente1.D11/MOSI
  GND: 8x8_LED_matrix_MAX1.GND_PT, 8x8_LED_matrix_MAX1.CLK, 8x8_LED_matrix_MAX2.GND, 8x8_LED_matrix_MAX2.CLK_PT, Componente1.GND, VCC1.-
  N2: 8x8_LED_matrix_MAX1.DIN, 8x8_LED_matrix_MAX2.DIN_CHN, 8x8_LED_matrix_MAX2.CS, Componente1.D10
  N3: 8x8_LED_matrix_MAX1.DIN_CHN, 8x8_LED_matrix_MAX1.CS, 8x8_LED_matrix_MAX2.CS_PT
  N4: 8x8_LED_matrix_MAX2.DIN, Componente1.D12/MISO
  N5: Componente1.VIN, S1.L2
  N6: VCC1.+, S1.COM

custom parts:
  8x8 Red 8x8 LED Matrix with MAX7219: Description: 8 by 8 red LED matrix with a MAX7219 controller.
